// Logisim project 6_CONG.circ as structural Verilog: 1 circuit, main circuit main
module main (
  input  \CỔNG_AND ,
  input  in_2,
  input  in_3,
  input  \CỔNG_OR ,
  input  in_5,
  input  in_6,
  input  in_7,
  input  in_8,
  input  \CỔNG_XOR ,
  input  in_10,
  input  in_11,
  output out_12,
  output out_13,
  output out_14,
  output out_15,
  output out_16,
  output out_17
);

  and and_1 (out_13, \CỔNG_AND , in_3);
  or or_1 (out_14, \CỔNG_OR , in_6);
  xor xor_1 (out_17, \CỔNG_XOR , in_11);
  not not_1 (out_12, in_2);
  nor nor_1 (out_15, in_5, in_7);
  nand nand_1 (out_16, in_8, in_10);

  // Notes on the sheet:
  //   CỔNG NOT(INVENTER)
  //   CỔNG NOR
  //   CỔNG NAND
endmodule
