// Logisim project FULL_HALF_ADDER.circ as structural Verilog: 1 circuit, main circuit main
module main (
  input  A1,
  input  A,
  input  B1,
  input  B,
  input  CIN,
  input  A2,
  input  B2,
  input  B_in
);

  wire and_1_out, and_2_out, and_3_out, and_4_out, and_5_out, not_1_out, not_2_out, or_1_out, or_2_out,
       xor_1_out, xor_2_out, xor_3_out, xor_4_out, xor_5_out;

  xor xor_1 (xor_1_out, A, B);
  and and_1 (and_1_out, B, A);
  // RGBLED SUM: pin names not known; wires that end beside it: xor_1_out
  LED CARRY (.in(and_1_out));
  xor xor_2 (xor_2_out, A2, B2);
  not not_1 (not_1_out, A2);
  not not_2 (not_2_out, xor_2_out);
  and and_2 (and_2_out, not_1_out, B2);
  xor xor_3 (xor_3_out, B_in, xor_2_out);
  LED D (.in(xor_3_out));
  and and_3 (and_3_out, not_2_out, B_in);
  xor xor_4 (xor_4_out, A1, B1);
  and and_4 (and_4_out, xor_4_out, CIN);
  or or_1 (or_1_out, and_3_out, and_2_out);
  LED B_out (.in(or_1_out));
  xor xor_5 (xor_5_out, xor_4_out, CIN);
  LED SUM1 (.in(xor_5_out));
  and and_5 (and_5_out, A1, B1);
  or or_2 (or_2_out, and_4_out, and_5_out);
  LED COUT (.in(or_2_out));

  // Notes on the sheet:
  //   HALF ADDER
  //   FULL SUBTRACTOR
  //   FULL ADDER
endmodule
